// Logisim project bad_apu.circ as structural Verilog: 1 circuit, main circuit main
module main (
);

  wire and_1_out, and_3_out, and_4_out, and_5_out, and_6_out, and_7_out, and_8_out, and_9_out, and_10_out,
       and_11_out, and_12_out, and_13_out, and_14_out, and_15_out, and_16_out, and_17_out, and_18_out,
       and_19_out, and_20_out, and_21_out, and_22_out, and_23_out, and_24_out, and_25_out, and_26_out,
       and_27_out, and_28_out, and_29_out, and_30_out, and_31_out, and_32_out, and_33_out, and_34_out,
       and_35_out, and_36_out, and_37_out, and_38_out, and_39_out, and_40_out, and_41_out, and_42_out,
       and_43_out, and_44_out, and_45_out, and_46_out, and_47_out, and_48_out, and_49_out, and_50_out,
       and_51_out, and_52_out, and_53_out, and_54_out, and_55_out, and_56_out, and_57_out, and_58_out,
       and_59_out, and_60_out, and_61_out, and_62_out, and_63_out, and_64_out, and_65_out, and_66_out,
       and_67_out, and_68_out, and_69_out, and_70_out, bit_extender_2_out, comparator_1_eq, comparator_1_gt,
       comparator_1_lt, comparator_2_gt, comparator_2_lt, comparator_3_gt, decoder_1_out0, decoder_1_out1,
       decoder_1_out2, decoder_1_out3, decoder_1_out4, decoder_1_out5, decoder_1_out6, decoder_1_out7,
       decoder_1_out8, decoder_1_out9, decoder_1_out10, decoder_1_out11, decoder_1_out12, decoder_1_out13,
       decoder_1_out14, decoder_2_out0, decoder_2_out1, decoder_2_out2, decoder_2_out3, decoder_3_out0,
       decoder_3_out1, decoder_3_out2, decoder_3_out3, decoder_4_out0, decoder_4_out1, decoder_4_out2,
       decoder_4_out3, decoder_4_out4, decoder_4_out5, decoder_4_out6, decoder_4_out7, decoder_4_out8,
       decoder_4_out9, decoder_4_out10, decoder_4_out11, decoder_4_out12, decoder_4_out13, decoder_4_out14,
       decoder_4_out15, decoder_4_out16, decoder_4_out17, decoder_4_out18, decoder_4_out19, decoder_4_out20,
       decoder_4_out21, decoder_4_out22, decoder_4_out23, decoder_4_out24, decoder_4_out25, decoder_4_out26,
       decoder_4_out27, decoder_4_out28, decoder_4_out29, decoder_4_out30, decoder_4_out31, decoder_4_out32,
       decoder_4_out33, decoder_4_out34, decoder_4_out35, decoder_4_out36, decoder_4_out37, decoder_4_out38,
       decoder_4_out39, decoder_4_out40, decoder_4_out41, decoder_4_out42, decoder_4_out43, decoder_4_out44,
       decoder_4_out45, decoder_4_out46, decoder_4_out47, decoder_4_out50, decoder_4_out51, decoder_4_out52,
       decoder_4_out53, decoder_4_out54, decoder_4_out55, decoder_4_out56, decoder_4_out57, decoder_4_out58,
       decoder_4_out59, decoder_4_out60, decoder_4_out61, decoder_4_out62, decoder_4_out63, MainClock_out,
       multiplexer_6_out, not_1_out, not_3_out, not_4_out, not_5_out, or_1_out, or_3_out, or_4_out, or_5_out,
       or_6_out, undriven;
  wire [1:0] bit_extender_4_out, decoder_4_out48, InstructionMemory_data_3, not_6_out;
  wire [3:0] bit_extender_1_out, InstructionMemory_data_2;
  wire [5:0] bit_extender_3_out;
  wire [15:0] adder_1_out, adder_2_out, adder_3_out, and_2_out, bitselector_1_out, divider_1_out,
       divider_2_out, divider_2_rem, divider_3_out, divider_3_rem, MainMemory_dout, multiplexer_1_out,
       multiplexer_2_out, multiplexer_3_out, multiplexer_4_out, multiplexer_5_out, multiplexer_7_out,
       multiplexer_8_out, multiplexer_9_out, multiplexer_10_out, multiplexer_11_out, multiplexer_12_out,
       multiplexer_13_out, multiplexer_14_out, multiplexer_14_out_2, multiplexer_14_out_3,
       multiplexer_14_out_4, multiplier_1_out, multiplier_2_out, not_2_out, or_2_out, ProgramCounter_q,
       random_1_out, shifter_1_out, shifter_2_out, shifter_3_out, subtractor_1_out, X0_q, X1_q, X2_q, X3_q,
       X4_q, X5_q, X6_q, X7_q, X8_q, X9_q, X10_q, X11_q, X12_q, X13_q, X14_q, xnor_1_out, xor_1_out, XZR_q;
  wire [31:6] InstructionMemory_data;
  wire [63:0] register_1_q, register_2_q, register_3_q, register_4_q, register_5_q, register_6_q,
       register_7_q, register_8_q, register_9_q, register_10_q, register_11_q, register_12_q, register_13_q,
       register_14_q, register_15_q, register_16_q, register_17_q, register_18_q, register_19_q,
       register_20_q, register_21_q, register_22_q, register_23_q, register_24_q, register_25_q,
       register_26_q, register_27_q, register_28_q, register_29_q, register_30_q, register_31_q,
       register_32_q, register_33_q, register_34_q, register_35_q, register_36_q, register_37_q,
       register_38_q, register_39_q, register_40_q, register_41_q, register_42_q, register_43_q,
       register_44_q, register_45_q, register_46_q, register_47_q, register_48_q;

  Register #(.width(16)) ProgramCounter (
    .D(adder_3_out), .en(1'b1), .clk(MainClock_out), .Q(ProgramCounter_q));  // open: clr
  ROM #(.addrWidth(16), .dataWidth(32)) InstructionMemory (
    .addr(ProgramCounter_q),
    .data({InstructionMemory_data, InstructionMemory_data_2, InstructionMemory_data_3}));
  Multiplexer #(.select(4), .width(16)) multiplexer_1 (
    .in0(X0_q), .in1(X1_q), .in2(X2_q), .in3(X3_q), .in4(X4_q), .in5(X5_q), .in6(X6_q), .in7(X7_q),
    .in8(X8_q), .in9(X9_q), .in10(X10_q), .in11(X11_q), .in12(X12_q), .in13(X13_q), .in14(X14_q),
    .in15(XZR_q), .out(multiplexer_1_out), .sel(InstructionMemory_data[14:11]));
  // Probe on multiplexer_1_out
  // Probe on multiplexer_3_out
  Bit_Extender #(.in_width(16), .out_width(4)) bit_extender_1 (.in(multiplexer_3_out), .out(bit_extender_1_out));
  // Probe on bit_extender_1_out
  Decoder #(.enable("false"), .select(4)) decoder_1 (
    .out0(decoder_1_out0), .out1(decoder_1_out1), .out2(decoder_1_out2), .out3(decoder_1_out3),
    .out4(decoder_1_out4), .out5(decoder_1_out5), .out6(decoder_1_out6), .out7(decoder_1_out7),
    .out8(decoder_1_out8), .out9(decoder_1_out9), .out10(decoder_1_out10), .out11(decoder_1_out11),
    .out12(decoder_1_out12), .out13(decoder_1_out13), .out14(decoder_1_out14),
    .sel(InstructionMemory_data[10:7]));  // open: out15
  Multiplexer #(.select(4), .width(16)) multiplexer_2 (
    .in0(X0_q), .in1(X1_q), .in2(X2_q), .in3(X3_q), .in4(X4_q), .in5(X5_q), .in6(X6_q), .in7(X7_q),
    .in8(X8_q), .in9(X9_q), .in10(X10_q), .in11(X11_q), .in12(X12_q), .in13(X13_q), .in14(X14_q),
    .in15(XZR_q), .out(multiplexer_2_out), .sel(InstructionMemory_data[10:7]));
  not not_1 (not_1_out, bit_extender_2_out);
  and and_1 (and_1_out, not_1_out, decoder_2_out2);
  or or_1 (or_1_out, and_1_out, and_20_out, decoder_2_out0);
  // Probe on InstructionMemory_data[10:7]
  // Probe on multiplexer_2_out
  Random #(.width(16)) random_1 (.next(1'b1), .clk(MainClock_out), .out(random_1_out));  // open: clr
  Adder #(.width(16)) adder_1 (.a(multiplexer_1_out), .b(multiplexer_3_out), .out(adder_1_out));  // open: cin, cout
  Subtractor #(.width(16)) subtractor_1 (
    .a(multiplexer_1_out), .b(multiplexer_3_out), .out(subtractor_1_out));  // open: bin, bout
  Multiplier #(.width(16)) multiplier_1 (
    .a(multiplexer_1_out), .b(multiplexer_3_out), .out(multiplier_1_out));  // open: cin, cout
  Multiplier #(.width(16)) multiplier_2 (
    .a(multiplexer_1_out), .b(multiplexer_3_out), .out(multiplier_2_out));  // open: cin, cout
  Divider #(.width(16)) divider_1 (
    .a(multiplexer_1_out), .b(multiplexer_3_out), .out(divider_1_out));  // open: upper, rem
  Divider #(.mode("twosComplement"), .width(16)) divider_2 (
    .a(multiplexer_1_out), .b(multiplexer_3_out), .out(divider_2_out), .rem(divider_2_rem));  // open: upper
  assign not_2_out = ~multiplexer_1_out;  // NOT_Gate not_2, 16 bits wide
  assign and_2_out = multiplexer_1_out & multiplexer_3_out;  // AND_Gate and_2, 16 bits wide
  assign or_2_out = multiplexer_1_out | multiplexer_3_out;  // OR_Gate or_2, 16 bits wide
  assign xor_1_out = multiplexer_1_out ^ multiplexer_3_out;  // XOR_Gate xor_1, 16 bits wide
  assign xnor_1_out = ~(multiplexer_1_out ^ multiplexer_3_out);  // XNOR_Gate xnor_1, 16 bits wide
  Shifter #(.width(16)) shifter_1 (.in(multiplexer_1_out), .\dist (bit_extender_1_out), .out(shifter_1_out));
  Shifter #(.shift("lr"), .width(16)) shifter_2 (
    .in(multiplexer_1_out), .\dist (bit_extender_1_out), .out(shifter_2_out));
  Shifter #(.shift("ar"), .width(16)) shifter_3 (
    .in(multiplexer_1_out), .\dist (bit_extender_1_out), .out(shifter_3_out));
  Multiplexer #(.width(16)) multiplexer_3 (
    .in0(InstructionMemory_data[31:16]), .in1(multiplexer_4_out), .out(multiplexer_3_out),
    .sel(InstructionMemory_data[15]));
  // Probe on adder_1_out
  // Probe on subtractor_1_out
  // Probe on multiplier_1_out
  // Probe on multiplier_2_out
  // Probe on divider_1_out
  // Probe on divider_2_out
  // Probe on divider_2_rem
  // Probe on not_2_out
  // Probe on and_2_out
  // Probe on or_2_out
  // Probe on xor_1_out
  // Probe on xnor_1_out
  // Probe on random_1_out
  // Probe on shifter_1_out
  // Probe on shifter_2_out
  // Probe on shifter_3_out
  Register #(.width(16)) X0 (.D(multiplexer_7_out), .en(and_3_out), .clk(MainClock_out), .Q(X0_q));  // open: clr
  and and_3 (and_3_out, decoder_1_out0, or_1_out);
  Register #(.width(16)) X4 (.D(multiplexer_7_out), .en(and_4_out), .clk(MainClock_out), .Q(X4_q));  // open: clr
  and and_4 (and_4_out, decoder_1_out4, or_1_out);
  Register #(.width(16)) X8 (.D(multiplexer_7_out), .en(and_5_out), .clk(MainClock_out), .Q(X8_q));  // open: clr
  and and_5 (and_5_out, decoder_1_out8, or_1_out);
  Register #(.width(16)) X12 (.D(multiplexer_7_out), .en(and_6_out), .clk(MainClock_out), .Q(X12_q));  // open: clr
  and and_6 (and_6_out, decoder_1_out12, or_1_out);
  Multiplexer #(.select(4), .width(16)) multiplexer_4 (
    .in0(X0_q), .in1(X1_q), .in2(X2_q), .in3(X3_q), .in4(X4_q), .in5(X5_q), .in6(X6_q), .in7(X7_q),
    .in8(X8_q), .in9(X9_q), .in10(X10_q), .in11(X11_q), .in12(X12_q), .in13(X13_q), .in14(X14_q),
    .in15(XZR_q), .out(multiplexer_4_out), .sel(InstructionMemory_data[19:16]));
  // Probe on multiplexer_4_out
  Decoder #(.enable("false"), .select(2)) decoder_2 (
    .out0(decoder_2_out0), .out1(decoder_2_out1), .out2(decoder_2_out2), .out3(decoder_2_out3),
    .sel(InstructionMemory_data_3));
  Bit_Extender #(.in_width(4), .out_width(1)) bit_extender_2 (.in(InstructionMemory_data_2), .out(bit_extender_2_out));
  Register #(.width(16)) X1 (.D(multiplexer_7_out), .en(and_7_out), .clk(MainClock_out), .Q(X1_q));  // open: clr
  and and_7 (and_7_out, decoder_1_out1, or_1_out);
  Register #(.width(16)) X5 (.D(multiplexer_7_out), .en(and_8_out), .clk(MainClock_out), .Q(X5_q));  // open: clr
  and and_8 (and_8_out, decoder_1_out5, or_1_out);
  Register #(.width(16)) X9 (.D(multiplexer_7_out), .en(and_9_out), .clk(MainClock_out), .Q(X9_q));  // open: clr
  and and_9 (and_9_out, decoder_1_out9, or_1_out);
  Register #(.width(16)) X13 (.D(multiplexer_7_out), .en(and_10_out), .clk(MainClock_out), .Q(X13_q));  // open: clr
  and and_10 (and_10_out, decoder_1_out13, or_1_out);
  // Probe on InstructionMemory_data[31:16]
  Register #(.width(16)) X2 (.D(multiplexer_7_out), .en(and_11_out), .clk(MainClock_out), .Q(X2_q));  // open: clr
  and and_11 (and_11_out, decoder_1_out2, or_1_out);
  Register #(.width(16)) X6 (.D(multiplexer_7_out), .en(and_12_out), .clk(MainClock_out), .Q(X6_q));  // open: clr
  and and_12 (and_12_out, decoder_1_out6, or_1_out);
  Register #(.width(16)) X10 (.D(multiplexer_7_out), .en(and_13_out), .clk(MainClock_out), .Q(X10_q));  // open: clr
  and and_13 (and_13_out, decoder_1_out10, or_1_out);
  Register #(.width(16)) X14 (.D(multiplexer_7_out), .en(and_14_out), .clk(MainClock_out), .Q(X14_q));  // open: clr
  and and_14 (and_14_out, decoder_1_out14, or_1_out);
  // Probe on InstructionMemory_data_2
  Multiplexer #(.select(4), .width(16)) multiplexer_5 (
    .in0(adder_1_out), .in1(subtractor_1_out), .in2(multiplier_1_out), .in3(multiplier_2_out),
    .in4(divider_1_out), .in5(divider_2_out), .in6(divider_2_rem), .in7(not_2_out), .in8(and_2_out),
    .in9(or_2_out), .in10(xor_1_out), .in11(xnor_1_out), .in12(random_1_out), .in13(shifter_1_out),
    .in14(shifter_2_out), .in15(shifter_3_out), .out(multiplexer_5_out), .sel(InstructionMemory_data_2));
  // Probe on InstructionMemory_data[14:11]
  // Probe on multiplexer_5_out
  Comparator #(.width(16)) comparator_1 (
    .a(multiplexer_1_out), .b(multiplexer_2_out), .gt(comparator_1_gt), .eq(comparator_1_eq),
    .lt(comparator_1_lt));
  Comparator #(.mode("unsigned"), .width(16)) comparator_2 (
    .a(multiplexer_1_out), .b(multiplexer_2_out), .gt(comparator_2_gt), .lt(comparator_2_lt));  // open: eq
  Register #(.width(16)) X3 (.D(multiplexer_7_out), .en(and_15_out), .clk(MainClock_out), .Q(X3_q));  // open: clr
  and and_15 (and_15_out, decoder_1_out3, or_1_out);
  Register #(.width(16)) X7 (.D(multiplexer_7_out), .en(and_16_out), .clk(MainClock_out), .Q(X7_q));  // open: clr
  and and_16 (and_16_out, decoder_1_out7, or_1_out);
  Register #(.width(16)) X11 (.D(multiplexer_7_out), .en(and_17_out), .clk(MainClock_out), .Q(X11_q));  // open: clr
  and and_17 (and_17_out, decoder_1_out11, or_1_out);
  Register #(.width(16)) XZR (.Q(XZR_q), .clr(undriven));  // open: D, en, clk
  not not_3 (not_3_out, bit_extender_2_out);
  and and_18 (and_18_out, bit_extender_2_out, decoder_2_out2);
  and and_19 (and_19_out, not_3_out, decoder_2_out2);
  // Probe on InstructionMemory_data[10:7]
  // Probe on adder_2_out
  Adder #(.width(16)) adder_2 (.a(multiplexer_1_out), .b(multiplexer_3_out), .out(adder_2_out));  // open: cin, cout
  not not_4 (not_4_out, comparator_1_eq);
  or or_3 (or_3_out, comparator_1_lt, comparator_1_eq);
  or or_4 (or_4_out, comparator_1_eq, comparator_1_gt);
  or or_5 (or_5_out, comparator_1_eq, comparator_2_lt);
  or or_6 (or_6_out, comparator_1_eq, comparator_2_gt);
  Clock MainClock (.out(MainClock_out));
  // Probe on InstructionMemory_data[31:16]
  // Probe on multiplexer_7_out
  // Probe on InstructionMemory_data_2
  Multiplexer #(.select(4)) multiplexer_6 (
    .in0(1'b1), .in1(comparator_1_eq), .in2(not_4_out), .in3(comparator_1_lt), .in4(or_3_out),
    .in5(comparator_1_gt), .in6(or_4_out), .in7(comparator_2_lt), .in8(or_5_out), .in9(comparator_2_gt),
    .in10(or_6_out), .in11(1'b0), .in12(1'b0), .in13(1'b0), .in14(1'b0), .in15(1'b0),
    .out(multiplexer_6_out), .sel(InstructionMemory_data_2));
  not not_5 (not_5_out, bit_extender_2_out);
  and and_20 (and_20_out, not_5_out, decoder_2_out3);
  RAM #(.addrWidth(16), .asyncread("true"), .dataWidth(16), .\type ("nonvolatile")) MainMemory (
    .addr(adder_2_out), .we(and_18_out), .oe(and_19_out), .clk(MainClock_out), .din(multiplexer_2_out),
    .dout(MainMemory_dout));
  and and_21 (and_21_out, decoder_2_out3, bit_extender_2_out);
  // Probe on MainMemory_dout
  // Probe on adder_2_out
  // Probe on multiplexer_2_out
  // Probe on bitselector_1_out
  Multiplexer #(.width(16)) multiplexer_7 (
    .in0(multiplexer_8_out), .in1(bitselector_1_out), .out(multiplexer_7_out), .sel(and_20_out));
  Multiplexer #(.width(16)) multiplexer_8 (
    .in0(multiplexer_5_out), .in1(MainMemory_dout), .out(multiplexer_8_out), .sel(and_19_out));
  BitSelector #(.group(16), .width(64)) bitselector_1 (
    .in({multiplexer_14_out_4, multiplexer_14_out_3, multiplexer_14_out_2, multiplexer_14_out}),
    .out(bitselector_1_out), .sel(not_6_out));
  // Probe on ProgramCounter_q
  Multiplexer #(.width(16)) multiplexer_9 (
    .in0(16'h1), .in1(InstructionMemory_data[31:16]), .out(multiplexer_9_out), .sel(and_22_out));
  // Probe on comparator_3_gt
  Comparator #(.mode("unsigned"), .width(16)) comparator_3 (
    .a(adder_2_out), .b(16'hc0), .gt(comparator_3_gt));  // open: eq, lt
  // Probe on adder_3_out
  Adder #(.width(16)) adder_3 (.a(ProgramCounter_q), .b(multiplexer_9_out), .out(adder_3_out));  // open: cin, cout
  and and_22 (and_22_out, multiplexer_6_out, decoder_2_out1);
  Divider #(.width(16)) divider_3 (
    .a(adder_2_out), .b(16'h4), .out(divider_3_out), .rem(divider_3_rem));  // open: upper
  Multiplexer #(.width(16)) multiplexer_10 (
    .in0(multiplexer_14_out), .in1(multiplexer_2_out), .out(multiplexer_10_out), .sel(decoder_3_out0));
  Multiplexer #(.width(16)) multiplexer_11 (
    .in0(multiplexer_14_out_2), .in1(multiplexer_2_out), .out(multiplexer_11_out), .sel(decoder_3_out1));
  Multiplexer #(.width(16)) multiplexer_12 (
    .in0(multiplexer_14_out_3), .in1(multiplexer_2_out), .out(multiplexer_12_out), .sel(decoder_3_out2));
  Multiplexer #(.width(16)) multiplexer_13 (
    .in0(multiplexer_14_out_4), .in1(multiplexer_2_out), .out(multiplexer_13_out), .sel(decoder_3_out3));
  Bit_Extender #(.in_width(16), .out_width(6)) bit_extender_3 (.in(divider_3_out), .out(bit_extender_3_out));
  Bit_Extender #(.in_width(16), .out_width(2)) bit_extender_4 (.in(divider_3_rem), .out(bit_extender_4_out));
  assign not_6_out = ~bit_extender_4_out;  // NOT_Gate not_6, 2 bits wide
  Decoder #(.enable("false"), .select(2)) decoder_3 (
    .out0(decoder_3_out0), .out1(decoder_3_out1), .out2(decoder_3_out2), .out3(decoder_3_out3),
    .sel(not_6_out));
  // Probe on bit_extender_4_out
  // Probe on {multiplexer_13_out, multiplexer_12_out, multiplexer_11_out, multiplexer_10_out}
  // Probe on {multiplexer_14_out_4, multiplexer_14_out_3, multiplexer_14_out_2, multiplexer_14_out}
  // Probe on bit_extender_3_out
  Decoder #(.enable("false"), .select(6)) decoder_4 (
    .out0(decoder_4_out0), .out1(decoder_4_out1), .out2(decoder_4_out2), .out3(decoder_4_out3),
    .out4(decoder_4_out4), .out5(decoder_4_out5), .out6(decoder_4_out6), .out7(decoder_4_out7),
    .out8(decoder_4_out8), .out9(decoder_4_out9), .out10(decoder_4_out10), .out11(decoder_4_out11),
    .out12(decoder_4_out12), .out13(decoder_4_out13), .out14(decoder_4_out14), .out15(decoder_4_out15),
    .out16(decoder_4_out16), .out17(decoder_4_out17), .out18(decoder_4_out18), .out19(decoder_4_out19),
    .out20(decoder_4_out20), .out21(decoder_4_out21), .out22(decoder_4_out22), .out23(decoder_4_out23),
    .out24(decoder_4_out24), .out25(decoder_4_out25), .out26(decoder_4_out26), .out27(decoder_4_out27),
    .out28(decoder_4_out28), .out29(decoder_4_out29), .out30(decoder_4_out30), .out31(decoder_4_out31),
    .out32(decoder_4_out32), .out33(decoder_4_out33), .out34(decoder_4_out34), .out35(decoder_4_out35),
    .out36(decoder_4_out36), .out37(decoder_4_out37), .out38(decoder_4_out38), .out39(decoder_4_out39),
    .out40(decoder_4_out40), .out41(decoder_4_out41), .out42(decoder_4_out42), .out43(decoder_4_out43),
    .out44(decoder_4_out44), .out45(decoder_4_out45), .out46(decoder_4_out46), .out47(decoder_4_out47),
    .out48(decoder_4_out48[0]), .out49(decoder_4_out48[1]), .out50(decoder_4_out50), .out51(decoder_4_out51),
    .out52(decoder_4_out52), .out53(decoder_4_out53), .out54(decoder_4_out54), .out55(decoder_4_out55),
    .out56(decoder_4_out56), .out57(decoder_4_out57), .out58(decoder_4_out58), .out59(decoder_4_out59),
    .out60(decoder_4_out60), .out61(decoder_4_out61), .out62(decoder_4_out62), .out63(decoder_4_out63),
    .sel(bit_extender_3_out));
  // Probe on decoder_4_out48
  Register #(.width(64)) register_1 (
    .D({multiplexer_13_out, multiplexer_12_out, multiplexer_11_out, multiplexer_10_out}), .en(and_23_out),
    .clk(MainClock_out), .Q(register_1_q));  // open: clr
  and and_23 (and_23_out, and_21_out, decoder_4_out0);
  Register #(.width(64)) register_2 (
    .D({multiplexer_13_out, multiplexer_12_out, multiplexer_11_out, multiplexer_10_out}), .en(and_24_out),
    .clk(MainClock_out), .Q(register_2_q));  // open: clr
  and and_24 (and_24_out, and_21_out, decoder_4_out8);
  Register #(.width(64)) register_3 (
    .D({multiplexer_13_out, multiplexer_12_out, multiplexer_11_out, multiplexer_10_out}), .en(and_25_out),
    .clk(MainClock_out), .Q(register_3_q));  // open: clr
  and and_25 (and_25_out, and_21_out, decoder_4_out16);
  Register #(.width(64)) register_4 (
    .D({multiplexer_13_out, multiplexer_12_out, multiplexer_11_out, multiplexer_10_out}), .en(and_26_out),
    .clk(MainClock_out), .Q(register_4_q));  // open: clr
  and and_26 (and_26_out, and_21_out, decoder_4_out24);
  Register #(.width(64)) register_5 (
    .D({multiplexer_13_out, multiplexer_12_out, multiplexer_11_out, multiplexer_10_out}), .en(and_27_out),
    .clk(MainClock_out), .Q(register_5_q));  // open: clr
  and and_27 (and_27_out, and_21_out, decoder_4_out32);
  Register #(.width(64)) register_6 (
    .D({multiplexer_13_out, multiplexer_12_out, multiplexer_11_out, multiplexer_10_out}), .en(and_28_out),
    .clk(MainClock_out), .Q(register_6_q));  // open: clr
  and and_28 (and_28_out, and_21_out, decoder_4_out40);
  Register #(.width(64)) register_7 (
    .D({multiplexer_13_out, multiplexer_12_out, multiplexer_11_out, multiplexer_10_out}), .en(and_29_out),
    .clk(MainClock_out), .Q(register_7_q));  // open: clr
  and and_29 (and_29_out, and_21_out, decoder_4_out1);
  Register #(.width(64)) register_8 (
    .D({multiplexer_13_out, multiplexer_12_out, multiplexer_11_out, multiplexer_10_out}), .en(and_30_out),
    .clk(MainClock_out), .Q(register_8_q));  // open: clr
  and and_30 (and_30_out, and_21_out, decoder_4_out9);
  Register #(.width(64)) register_9 (
    .D({multiplexer_13_out, multiplexer_12_out, multiplexer_11_out, multiplexer_10_out}), .en(and_31_out),
    .clk(MainClock_out), .Q(register_9_q));  // open: clr
  and and_31 (and_31_out, and_21_out, decoder_4_out17);
  Register #(.width(64)) register_10 (
    .D({multiplexer_13_out, multiplexer_12_out, multiplexer_11_out, multiplexer_10_out}), .en(and_32_out),
    .clk(MainClock_out), .Q(register_10_q));  // open: clr
  and and_32 (and_32_out, and_21_out, decoder_4_out25);
  Register #(.width(64)) register_11 (
    .D({multiplexer_13_out, multiplexer_12_out, multiplexer_11_out, multiplexer_10_out}), .en(and_33_out),
    .clk(MainClock_out), .Q(register_11_q));  // open: clr
  and and_33 (and_33_out, and_21_out, decoder_4_out33);
  Register #(.width(64)) register_12 (
    .D({multiplexer_13_out, multiplexer_12_out, multiplexer_11_out, multiplexer_10_out}), .en(and_34_out),
    .clk(MainClock_out), .Q(register_12_q));  // open: clr
  and and_34 (and_34_out, and_21_out, decoder_4_out41);
  Register #(.width(64)) register_13 (
    .D({multiplexer_13_out, multiplexer_12_out, multiplexer_11_out, multiplexer_10_out}), .en(and_35_out),
    .clk(MainClock_out), .Q(register_13_q));  // open: clr
  and and_35 (and_35_out, and_21_out, decoder_4_out2);
  Register #(.width(64)) register_14 (
    .D({multiplexer_13_out, multiplexer_12_out, multiplexer_11_out, multiplexer_10_out}), .en(and_36_out),
    .clk(MainClock_out), .Q(register_14_q));  // open: clr
  and and_36 (and_36_out, and_21_out, decoder_4_out10);
  Register #(.width(64)) register_15 (
    .D({multiplexer_13_out, multiplexer_12_out, multiplexer_11_out, multiplexer_10_out}), .en(and_37_out),
    .clk(MainClock_out), .Q(register_15_q));  // open: clr
  and and_37 (and_37_out, and_21_out, decoder_4_out18);
  Register #(.width(64)) register_16 (
    .D({multiplexer_13_out, multiplexer_12_out, multiplexer_11_out, multiplexer_10_out}), .en(and_38_out),
    .clk(MainClock_out), .Q(register_16_q));  // open: clr
  and and_38 (and_38_out, and_21_out, decoder_4_out26);
  Register #(.width(64)) register_17 (
    .D({multiplexer_13_out, multiplexer_12_out, multiplexer_11_out, multiplexer_10_out}), .en(and_39_out),
    .clk(MainClock_out), .Q(register_17_q));  // open: clr
  and and_39 (and_39_out, and_21_out, decoder_4_out34);
  Register #(.width(64)) register_18 (
    .D({multiplexer_13_out, multiplexer_12_out, multiplexer_11_out, multiplexer_10_out}), .en(and_40_out),
    .clk(MainClock_out), .Q(register_18_q));  // open: clr
  and and_40 (and_40_out, and_21_out, decoder_4_out42);
  Register #(.width(64)) register_19 (
    .D({multiplexer_13_out, multiplexer_12_out, multiplexer_11_out, multiplexer_10_out}), .en(and_41_out),
    .clk(MainClock_out), .Q(register_19_q));  // open: clr
  and and_41 (and_41_out, and_21_out, decoder_4_out3);
  Register #(.width(64)) register_20 (
    .D({multiplexer_13_out, multiplexer_12_out, multiplexer_11_out, multiplexer_10_out}), .en(and_42_out),
    .clk(MainClock_out), .Q(register_20_q));  // open: clr
  and and_42 (and_42_out, and_21_out, decoder_4_out11);
  Register #(.width(64)) register_21 (
    .D({multiplexer_13_out, multiplexer_12_out, multiplexer_11_out, multiplexer_10_out}), .en(and_43_out),
    .clk(MainClock_out), .Q(register_21_q));  // open: clr
  and and_43 (and_43_out, and_21_out, decoder_4_out19);
  Register #(.width(64)) register_22 (
    .D({multiplexer_13_out, multiplexer_12_out, multiplexer_11_out, multiplexer_10_out}), .en(and_44_out),
    .clk(MainClock_out), .Q(register_22_q));  // open: clr
  and and_44 (and_44_out, and_21_out, decoder_4_out27);
  Register #(.width(64)) register_23 (
    .D({multiplexer_13_out, multiplexer_12_out, multiplexer_11_out, multiplexer_10_out}), .en(and_45_out),
    .clk(MainClock_out), .Q(register_23_q));  // open: clr
  and and_45 (and_45_out, and_21_out, decoder_4_out35);
  Register #(.width(64)) register_24 (
    .D({multiplexer_13_out, multiplexer_12_out, multiplexer_11_out, multiplexer_10_out}), .en(and_46_out),
    .clk(MainClock_out), .Q(register_24_q));  // open: clr
  and and_46 (and_46_out, and_21_out, decoder_4_out43);
  Register #(.width(64)) register_25 (
    .D({multiplexer_13_out, multiplexer_12_out, multiplexer_11_out, multiplexer_10_out}), .en(and_47_out),
    .clk(MainClock_out), .Q(register_25_q));  // open: clr
  and and_47 (and_47_out, and_21_out, decoder_4_out4);
  Register #(.width(64)) register_26 (
    .D({multiplexer_13_out, multiplexer_12_out, multiplexer_11_out, multiplexer_10_out}), .en(and_48_out),
    .clk(MainClock_out), .Q(register_26_q));  // open: clr
  and and_48 (and_48_out, and_21_out, decoder_4_out12);
  Register #(.width(64)) register_27 (
    .D({multiplexer_13_out, multiplexer_12_out, multiplexer_11_out, multiplexer_10_out}), .en(and_49_out),
    .clk(MainClock_out), .Q(register_27_q));  // open: clr
  and and_49 (and_49_out, and_21_out, decoder_4_out20);
  Register #(.width(64)) register_28 (
    .D({multiplexer_13_out, multiplexer_12_out, multiplexer_11_out, multiplexer_10_out}), .en(and_50_out),
    .clk(MainClock_out), .Q(register_28_q));  // open: clr
  and and_50 (and_50_out, and_21_out, decoder_4_out28);
  Register #(.width(64)) register_29 (
    .D({multiplexer_13_out, multiplexer_12_out, multiplexer_11_out, multiplexer_10_out}), .en(and_51_out),
    .clk(MainClock_out), .Q(register_29_q));  // open: clr
  and and_51 (and_51_out, and_21_out, decoder_4_out36);
  Register #(.width(64)) register_30 (
    .D({multiplexer_13_out, multiplexer_12_out, multiplexer_11_out, multiplexer_10_out}), .en(and_52_out),
    .clk(MainClock_out), .Q(register_30_q));  // open: clr
  and and_52 (and_52_out, and_21_out, decoder_4_out44);
  Register #(.width(64)) register_31 (
    .D({multiplexer_13_out, multiplexer_12_out, multiplexer_11_out, multiplexer_10_out}), .en(and_53_out),
    .clk(MainClock_out), .Q(register_31_q));  // open: clr
  and and_53 (and_53_out, and_21_out, decoder_4_out5);
  Register #(.width(64)) register_32 (
    .D({multiplexer_13_out, multiplexer_12_out, multiplexer_11_out, multiplexer_10_out}), .en(and_54_out),
    .clk(MainClock_out), .Q(register_32_q));  // open: clr
  and and_54 (and_54_out, and_21_out, decoder_4_out13);
  Register #(.width(64)) register_33 (
    .D({multiplexer_13_out, multiplexer_12_out, multiplexer_11_out, multiplexer_10_out}), .en(and_55_out),
    .clk(MainClock_out), .Q(register_33_q));  // open: clr
  and and_55 (and_55_out, and_21_out, decoder_4_out21);
  Register #(.width(64)) register_34 (
    .D({multiplexer_13_out, multiplexer_12_out, multiplexer_11_out, multiplexer_10_out}), .en(and_56_out),
    .clk(MainClock_out), .Q(register_34_q));  // open: clr
  and and_56 (and_56_out, and_21_out, decoder_4_out29);
  Register #(.width(64)) register_35 (
    .D({multiplexer_13_out, multiplexer_12_out, multiplexer_11_out, multiplexer_10_out}), .en(and_57_out),
    .clk(MainClock_out), .Q(register_35_q));  // open: clr
  and and_57 (and_57_out, and_21_out, decoder_4_out37);
  Register #(.width(64)) register_36 (
    .D({multiplexer_13_out, multiplexer_12_out, multiplexer_11_out, multiplexer_10_out}), .en(and_58_out),
    .clk(MainClock_out), .Q(register_36_q));  // open: clr
  and and_58 (and_58_out, and_21_out, decoder_4_out45);
  Register #(.width(64)) register_37 (
    .D({multiplexer_13_out, multiplexer_12_out, multiplexer_11_out, multiplexer_10_out}), .en(and_59_out),
    .clk(MainClock_out), .Q(register_37_q));  // open: clr
  and and_59 (and_59_out, and_21_out, decoder_4_out6);
  Register #(.width(64)) register_38 (
    .D({multiplexer_13_out, multiplexer_12_out, multiplexer_11_out, multiplexer_10_out}), .en(and_60_out),
    .clk(MainClock_out), .Q(register_38_q));  // open: clr
  and and_60 (and_60_out, and_21_out, decoder_4_out14);
  Register #(.width(64)) register_39 (
    .D({multiplexer_13_out, multiplexer_12_out, multiplexer_11_out, multiplexer_10_out}), .en(and_61_out),
    .clk(MainClock_out), .Q(register_39_q));  // open: clr
  and and_61 (and_61_out, and_21_out, decoder_4_out22);
  Register #(.width(64)) register_40 (
    .D({multiplexer_13_out, multiplexer_12_out, multiplexer_11_out, multiplexer_10_out}), .en(and_62_out),
    .clk(MainClock_out), .Q(register_40_q));  // open: clr
  and and_62 (and_62_out, and_21_out, decoder_4_out30);
  Register #(.width(64)) register_41 (
    .D({multiplexer_13_out, multiplexer_12_out, multiplexer_11_out, multiplexer_10_out}), .en(and_63_out),
    .clk(MainClock_out), .Q(register_41_q));  // open: clr
  and and_63 (and_63_out, and_21_out, decoder_4_out38);
  Register #(.width(64)) register_42 (
    .D({multiplexer_13_out, multiplexer_12_out, multiplexer_11_out, multiplexer_10_out}), .en(and_64_out),
    .clk(MainClock_out), .Q(register_42_q));  // open: clr
  and and_64 (and_64_out, and_21_out, decoder_4_out46);
  Register #(.width(64)) register_43 (
    .D({multiplexer_13_out, multiplexer_12_out, multiplexer_11_out, multiplexer_10_out}), .en(and_65_out),
    .clk(MainClock_out), .Q(register_43_q));  // open: clr
  and and_65 (and_65_out, and_21_out, decoder_4_out7);
  Register #(.width(64)) register_44 (
    .D({multiplexer_13_out, multiplexer_12_out, multiplexer_11_out, multiplexer_10_out}), .en(and_66_out),
    .clk(MainClock_out), .Q(register_44_q));  // open: clr
  and and_66 (and_66_out, and_21_out, decoder_4_out15);
  Register #(.width(64)) register_45 (
    .D({multiplexer_13_out, multiplexer_12_out, multiplexer_11_out, multiplexer_10_out}), .en(and_67_out),
    .clk(MainClock_out), .Q(register_45_q));  // open: clr
  and and_67 (and_67_out, and_21_out, decoder_4_out23);
  Register #(.width(64)) register_46 (
    .D({multiplexer_13_out, multiplexer_12_out, multiplexer_11_out, multiplexer_10_out}), .en(and_68_out),
    .clk(MainClock_out), .Q(register_46_q));  // open: clr
  and and_68 (and_68_out, and_21_out, decoder_4_out31);
  Register #(.width(64)) register_47 (
    .D({multiplexer_13_out, multiplexer_12_out, multiplexer_11_out, multiplexer_10_out}), .en(and_69_out),
    .clk(MainClock_out), .Q(register_47_q));  // open: clr
  and and_69 (and_69_out, and_21_out, decoder_4_out39);
  Register #(.width(64)) register_48 (
    .D({multiplexer_13_out, multiplexer_12_out, multiplexer_11_out, multiplexer_10_out}), .en(and_70_out),
    .clk(MainClock_out), .Q(register_48_q));  // open: clr
  and and_70 (and_70_out, and_21_out, decoder_4_out47);
  Multiplexer #(.select(6), .width(64)) multiplexer_14 (
    .in0(register_1_q), .in1(register_7_q), .in2(register_13_q), .in3(register_19_q), .in4(register_25_q),
    .in5(register_31_q), .in6(register_37_q), .in7(register_43_q), .in8(register_2_q), .in9(register_8_q),
    .in10(register_14_q), .in11(register_20_q), .in12(register_26_q), .in13(register_32_q),
    .in14(register_38_q), .in15(register_44_q), .in16(register_3_q), .in17(register_9_q),
    .in18(register_15_q), .in19(register_21_q), .in20(register_27_q), .in21(register_33_q),
    .in22(register_39_q), .in23(register_45_q), .in24(register_4_q), .in25(register_10_q),
    .in26(register_16_q), .in27(register_22_q), .in28(register_28_q), .in29(register_34_q),
    .in30(register_40_q), .in31(register_46_q), .in32(register_5_q), .in33(register_11_q),
    .in34(register_17_q), .in35(register_23_q), .in36(register_29_q), .in37(register_35_q),
    .in38(register_41_q), .in39(register_47_q), .in40(register_6_q), .in41(register_12_q),
    .in42(register_18_q), .in43(register_24_q), .in44(register_30_q), .in45(register_36_q),
    .in46(register_42_q), .in47(register_48_q), .in48({64{1'b0}}), .in49({64{1'b0}}), .in50({64{1'b0}}),
    .in51({64{1'b0}}), .in52({64{1'b0}}), .in53({64{1'b0}}), .in54({64{1'b0}}), .in55({64{1'b0}}),
    .in56({64{1'b0}}), .in57({64{1'b0}}), .in58({64{1'b0}}), .in59({64{1'b0}}), .in60({64{1'b0}}),
    .in61({64{1'b0}}), .in62({64{1'b0}}), .in63({64{1'b0}}),
    .out({multiplexer_14_out_4, multiplexer_14_out_3, multiplexer_14_out_2, multiplexer_14_out}),
    .sel(bit_extender_3_out));
  DotMatrix #(.dotshape("circle"), .inputtype("row"), .matrixcols(64), .matrixrows(48)) VideoOutput (
    .row0(register_1_q), .row1(register_7_q), .row2(register_13_q), .row3(register_19_q),
    .row4(register_25_q), .row5(register_31_q), .row6(register_37_q), .row7(register_43_q),
    .row8(register_2_q), .row9(register_8_q), .row10(register_14_q), .row11(register_20_q),
    .row12(register_26_q), .row13(register_32_q), .row14(register_38_q), .row15(register_44_q),
    .row16(register_3_q), .row17(register_9_q), .row18(register_15_q), .row19(register_21_q),
    .row20(register_27_q), .row21(register_33_q), .row22(register_39_q), .row23(register_45_q),
    .row24(register_4_q), .row25(register_10_q), .row26(register_16_q), .row27(register_22_q),
    .row28(register_28_q), .row29(register_34_q), .row30(register_40_q), .row31(register_46_q),
    .row32(register_5_q), .row33(register_11_q), .row34(register_17_q), .row35(register_23_q),
    .row36(register_29_q), .row37(register_35_q), .row38(register_41_q), .row39(register_47_q),
    .row40(register_6_q), .row41(register_12_q), .row42(register_18_q), .row43(register_24_q),
    .row44(register_30_q), .row45(register_36_q), .row46(register_42_q), .row47(register_48_q));

  // Notes on the sheet:
  //   ALU
  //   contents of InstructionMemory (hex, n*v repeats v):
  //   7800 f5867880 882 7900 28182 7a00 c007a80 7b00 61f89 11100 28182 fb31c 13320 101085 102390 102418
  //   3c83 80007d00 8d538 43789 fd51c acca0 27f81 acca4 3c87 11984 12200 5a218 ffec7f81
  //   Immed
  //   Wb
  //   Op1
  //   Op2
  //   Op3
  //   OpType
  //   Bad Apu - Miller Paule
  //   Arith
  //   OpCode
  //   Register File
  //   Brancher
  //   Store?
  //   UseRegisterAsImmed?
  //   Mem
  //   Load?
  //   UseRegForImmed
  //   Equal?
  //   Not Equal?
  //   Signed Less Than?
  //   Signed Greater Than?
  //   Branch
  //   Signed Less Than Or Equal To?
  //   Signed Greater Than Or Equal To?
  //   Unsigned Less Than?
  //   Unsigned Less Than Or Equal To?
  //   Unsigned Greater Than?
  //   Unsigned Greater Than Or Equal To?
  //   Draw
  //   UseMemForWriteBack
  //   GraphicMemoryWriteEnable
  //   Branch Output
  //   Branch?
  //   Branch Instruction
  //   UseVideoMemForWriteBack
  //   Row 0 -> Row 7
  //   Row 8 -> Row 15
  //   Row 16 -> Row 23
  //   Row 24 -> Row 31
  //   Row 32 -> Row 39
  //   Row 40 -> Row 47
  //   VideoMemory
endmodule
